// Logisim project alu.circ as structural Verilog: 22 circuits, main circuit alu_and
module alu (
  input  [31:0] A,
  input  [31:0] B,
  input  [3:0] ALUSel,
  output [31:0] Result
);

  wire [31:0] ALUadd, ALUand, ALUcnto, ALUdiv, ALUdivu, ALUmulh, ALUmulhu, ALUmult, ALUor, ALUremu, ALUsir,
       ALUslt, ALUsra, ALUsrl, ALUsub, ALUxor;

  alu_and alu_and_1 (.A(A), .B(B), .C(ALUand));
  alu_or alu_or_1 (.A(A), .B(B), .C(ALUor));
  alu_xor alu_xor_1 (.A(A), .B(B), .C(ALUxor));
  alu_add alu_add_1 (.A(A), .B(B), .C(ALUadd));
  alu_sub alu_sub_1 (.A(A), .B(B), .C(ALUsub));
  alu_mult alu_mult_1 (.A(A), .B(B), .C(ALUmult));
  alu_mulhu alu_mulhu_1 (.A(A), .B(B), .C(ALUmulhu));
  alu_mulh alu_mulh_1 (.A(A), .B(B), .C(ALUmulh));
  alu_divu alu_divu_1 (.A(A), .B(B), .C(ALUdivu));
  alu_div alu_div_1 (.A(A), .B(B), .C(ALUdiv));
  alu_remu alu_remu_1 (.A(A), .B(B), .C(ALUremu));
  alu_srl alu_srl_1 (.A(A), .B(B), .C(ALUsrl));
  alu_sra alu_sra_1 (.A(A), .B(B), .C(ALUsra));
  alu_slt alu_slt_1 (.A(A), .B(B), .C(ALUslt));
  alu_sir alu_sir_1 (.A(A), .B(B), .C(ALUsir));
  alu_cnto alu_cnto_1 (.A(A), .B(B), .C(ALUcnto));
  Multiplexer #(.select(4), .width(32), .enable("false")) multiplexer_1 (
    .in0(ALUand), .in1(ALUor), .in2(ALUxor), .in3(ALUadd), .in4(ALUsub), .in5(ALUmult), .in6(ALUmulhu),
    .in7(ALUmulh), .in8(ALUdivu), .in9(ALUdiv), .in10(ALUremu), .in11(ALUsrl), .in12(ALUsra), .in13(ALUslt),
    .in14(ALUsir), .in15(ALUcnto), .out(Result), .sel(ALUSel));

  // Notes on the sheet:
  //   INPUTS to your circuit
  //   DON'T CHANGE THE LOCATIONS OF THE INPUTS AND OUTPUTS!
  //   OUTPUT from your circuit
endmodule

module alu_and (
  input  [31:0] A,
  input  [31:0] B,
  output [31:0] C
);

  assign C = A & B;  // AND_Gate and_1, 32 bits wide
endmodule

module alu_or (
  input  [31:0] A,
  input  [31:0] B,
  output [31:0] C
);

  assign C = A | B;  // OR_Gate or_1, 32 bits wide
endmodule

module alu_xor (
  input  [31:0] A,
  input  [31:0] B,
  output [31:0] C
);

  assign C = A ^ B;  // XOR_Gate xor_1, 32 bits wide
endmodule

module alu_add (
  input  [31:0] A,
  input  [31:0] B,
  output [31:0] C
);

  Adder #(.width(32)) adder_1 (.a(A), .b(B), .out(C));  // open: cin, cout
endmodule

module alu_sub (
  input  [31:0] A,
  input  [31:0] B,
  output [31:0] C
);

  Subtractor #(.width(32)) subtractor_1 (.a(A), .b(B), .out(C));  // open: bin, bout
endmodule

module alu_mult (
  input  [31:0] A,
  input  [31:0] B,
  output [31:0] C
);

  Multiplier #(.width(32)) multiplier_1 (.a(A), .b(B), .out(C));  // open: cin, cout
endmodule

module alu_mulhu (
  input  [31:0] A,
  input  [31:0] B,
  output [31:0] C
);

  Multiplier #(.width(32)) multiplier_1 (.a(A), .b(B), .cout(C));  // open: out, cin
endmodule

module alu_mulh (
  input  [31:0] A,
  input  [31:0] B,
  output [31:0] C
);

  wire [31:0] multiplexer_1_out, multiplexer_2_out, multiplier_1_cout, subtractor_1_out;

  Multiplier #(.width(32)) multiplier_1 (.a(A), .b(B), .cout(multiplier_1_cout));  // open: out, cin
  Multiplexer #(.width(32), .enable("false")) multiplexer_1 (
    .in0({32{1'b0}}), .in1(A), .out(multiplexer_1_out), .sel(B[31]));
  Subtractor #(.width(32)) subtractor_1 (
    .a(multiplier_1_cout), .b(multiplexer_1_out), .out(subtractor_1_out));  // open: bin, bout
  Multiplexer #(.width(32), .enable("false")) multiplexer_2 (
    .in0({32{1'b0}}), .in1(B), .out(multiplexer_2_out), .sel(A[31]));
  Subtractor #(.width(32)) subtractor_2 (.a(subtractor_1_out), .b(multiplexer_2_out), .out(C));  // open: bin, bout

  // Other names for the same wires on the sheet: A_sign = A[31]; B_sign = B[31]
endmodule

module alu_divu (
  input  [31:0] A,
  input  [31:0] B,
  output [31:0] C
);

  Divider #(.width(32)) divider_1 (.a(A), .b(B), .out(C));  // open: upper, rem
endmodule

module alu_div (
  input  [31:0] A,
  input  [31:0] B,
  output [31:0] C
);

  wire Sign_out;
  wire [31:0] divider_1_out, multiplexer_1_out, multiplexer_2_out, negator_1_out, negator_2_out,
       negator_3_out;

  Negator #(.width(32)) negator_1 (.in(A), .out(negator_1_out));
  xor Sign (Sign_out, A[31], B[31]);
  Negator #(.width(32)) negator_2 (.in(B), .out(negator_2_out));
  Multiplexer #(.width(32), .enable("false")) multiplexer_1 (
    .in0(A), .in1(negator_1_out), .out(multiplexer_1_out), .sel(A[31]));
  Multiplexer #(.width(32), .enable("false")) multiplexer_2 (
    .in0(B), .in1(negator_2_out), .out(multiplexer_2_out), .sel(B[31]));
  Divider #(.width(32)) divider_1 (
    .a(multiplexer_1_out), .b(multiplexer_2_out), .out(divider_1_out));  // open: upper, rem
  Negator #(.width(32)) negator_3 (.in(divider_1_out), .out(negator_3_out));
  Multiplexer #(.width(32), .enable("false")) multiplexer_3 (
    .in0(divider_1_out), .in1(negator_3_out), .out(C), .sel(Sign_out));
endmodule

module alu_remu (
  input  [31:0] A,
  input  [31:0] B,
  output [31:0] C
);

  wire [31:0] divider_1_out, multiplier_1_out;

  Divider #(.width(32)) divider_1 (.a(A), .b(B), .out(divider_1_out));  // open: upper, rem
  Multiplier #(.width(32)) multiplier_1 (.a(divider_1_out), .b(B), .out(multiplier_1_out));  // open: cin, cout
  Subtractor #(.width(32)) subtractor_1 (.a(A), .b(multiplier_1_out), .out(C));  // open: bin, bout
endmodule

module alu_srl (
  input  [31:0] A,
  input  [31:0] B,
  output [31:0] C
);

  Shifter #(.width(32), .shift("lr")) shifter_1 (.in(A), .\dist (B[4:0]), .out(C));
endmodule

module alu_sra (
  input  [31:0] A,
  input  [31:0] B,
  output [31:0] C
);

  Shifter #(.width(32), .shift("ar")) shifter_1 (.in(A), .\dist (B[4:0]), .out(C));
endmodule

module alu_slt (
  input  [31:0] A,
  input  [31:0] B,
  output [31:0] C
);

  Comparator #(.width(32)) comparator_1 (.a(A), .b(B), .lt(C[0]));  // open: gt, eq

  assign C[31:1] = {31{1'b0}};
endmodule

module alu_sir (
  input  [31:0] A,
  input  [31:0] B,
  output [31:0] C
);

  Comparator #(.width(32)) comparator_1 (
    .a(A),
    .b({B[0], B[1], B[2], B[3], B[4], B[5], B[6], B[7], B[8], B[9], B[10], B[11], B[12], B[13], B[14], B[15], B[16], B[17], B[18], B[19], B[20], B[21], B[22], B[23], B[24], B[25], B[26], B[27], B[28], B[29], B[30], B[31]}),
    .eq(C[0]));  // open: gt, lt

  assign C[31:1] = {31{1'b0}};
endmodule

module alu_cnto (
  input  [31:0] A,
  input  [31:0] B,
  output [31:0] C
);

  wire [31:0] cnto_32_1_out_2, cnto_32_2_out_2;

  cnto_32 cnto_32_1 (.in_1(A), .out_2(cnto_32_1_out_2));
  cnto_32 cnto_32_2 (.in_1(B), .out_2(cnto_32_2_out_2));
  Adder #(.width(32)) adder_1 (.a(cnto_32_1_out_2), .b(cnto_32_2_out_2), .out(C));  // open: cin, cout
endmodule

module cnto_32 (
  input  [31:0] in_1,
  output [31:0] out_2
);

  wire [31:0] cnto_16_1_out_2, cnto_16_2_out_2;

  cnto_16 cnto_16_1 (.in_1(in_1[15:0]), .out_2(cnto_16_1_out_2));
  cnto_16 cnto_16_2 (.in_1(in_1[31:16]), .out_2(cnto_16_2_out_2));
  Adder #(.width(32)) adder_1 (.a(cnto_16_1_out_2), .b(cnto_16_2_out_2), .out(out_2));  // open: cin, cout
endmodule

module cnto_16 (
  input  [15:0] in_1,
  output [31:0] out_2
);

  wire [31:0] cnto_8_1_out_2, cnto_8_2_out_2;

  cnto_8 cnto_8_1 (.in_1(in_1[7:0]), .out_2(cnto_8_1_out_2));
  cnto_8 cnto_8_2 (.in_1(in_1[15:8]), .out_2(cnto_8_2_out_2));
  Adder #(.width(32)) adder_1 (.a(cnto_8_1_out_2), .b(cnto_8_2_out_2), .out(out_2));  // open: cin, cout
endmodule

module cnto_8 (
  input  [7:0] in_1,
  output [31:0] out_2
);

  wire [31:0] cnto_4_1_out_2, cnto_4_2_out_2;

  cnto_4 cnto_4_1 (.in_1(in_1[3:0]), .out_2(cnto_4_1_out_2));
  cnto_4 cnto_4_2 (.in_1(in_1[7:4]), .out_2(cnto_4_2_out_2));
  Adder #(.width(32)) adder_1 (.a(cnto_4_1_out_2), .b(cnto_4_2_out_2), .out(out_2));  // open: cin, cout
endmodule

module cnto_4 (
  input  [3:0] in_1,
  output [31:0] out_2
);

  wire [31:0] cnto_2_1_out_2, cnto_2_2_out_2;

  cnto_2 cnto_2_1 (.in_1(in_1[1:0]), .out_2(cnto_2_1_out_2));
  cnto_2 cnto_2_2 (.in_1(in_1[3:2]), .out_2(cnto_2_2_out_2));
  Adder #(.width(32)) adder_1 (.a(cnto_2_1_out_2), .b(cnto_2_2_out_2), .out(out_2));  // open: cin, cout
endmodule

module cnto_2 (
  input  [1:0] in_1,
  output [31:0] out_2
);

  Adder #(.width(32)) adder_1 (.a({{31{1'b0}}, in_1[0]}), .b({{31{1'b0}}, in_1[1]}), .out(out_2));  // open: cin, cout
endmodule
