// Logisim project cpu.circ as structural Verilog: 4 circuits, main circuit main
module main (
  input  [31:0] INSTRUCTION,
  input  CLOCK,
  output [31:0] FETCH_ADDRESS,
  output [31:0] ra,
  output [31:0] sp,
  output [31:0] t0,
  output [31:0] t1,
  output [31:0] t2,
  output [31:0] s0,
  output [31:0] s1,
  output [31:0] a0
);

  wire Asel, BrEq, BrLT, BrUn, Bsel, comparator_1_eq, comparator_1_lt, comparator_2_eq, comparator_2_lt,
       MemRW, PCsel, RegWEn;
  wire [1:0] WBsel;
  wire [2:0] Immsel;
  wire [3:0] ALUsel;
  wire [31:0] adder_1_out, ALUresult, DMEM_readdata, imm, INSTRUCTION_t, multiplexer_1_out,
       multiplexer_2_out, multiplexer_4_out, multiplexer_5_out, PCnext, PCnow, rs1data, rs2data, writeback;

  Adder #(.width(32)) adder_1 (.a(PCnext), .b(32'h4), .out(adder_1_out));  // open: cin, cout
  Multiplexer #(.width(32), .enable("false")) multiplexer_1 (
    .in0(adder_1_out), .in1(ALUresult), .out(multiplexer_1_out), .sel(PCsel));
  Multiplexer #(.width(32), .enable("false")) multiplexer_2 (
    .in0(INSTRUCTION), .in1({32{1'b0}}), .out(multiplexer_2_out), .sel(PCsel));
  Register #(.width(32)) PC (.D(multiplexer_1_out), .clk(CLOCK), .Q(PCnext));  // open: en, clr
  imm_gen imm_gen_1 (.Instr(INSTRUCTION_t), .imm_sel(Immsel), .immediate(imm));
  control control_1 (
    .instr(INSTRUCTION_t), .BrLT(BrLT), .BrEq(BrEq), .PCsel(PCsel), .Immsel(Immsel), .RegWEn(RegWEn),
    .Asel(Asel), .Bsel(Bsel), .ALUsel(ALUsel), .MemRW(MemRW), .WBsel(WBsel), .BrUn(BrUn));
  mem_main DMEM (.WriteAddr(ALUresult), .WriteData(rs2data), .MemRW(MemRW), .ReadData(DMEM_readdata), .clk(CLOCK));
  Register #(.width(32)) Pipeline (.D(multiplexer_2_out), .clk(CLOCK), .Q(INSTRUCTION_t));  // open: en, clr
  Divider #(.width(32)) divider_1 (.a(PCnext), .b(32'h4), .out(FETCH_ADDRESS));  // open: upper, rem
  Multiplexer #(.select(2), .width(32), .enable("false")) multiplexer_3 (
    .in0(DMEM_readdata), .in1(ALUresult), .in2(PCnext), .out(writeback), .sel(WBsel));  // open: in3
  Subtractor #(.width(32)) subtractor_1 (.a(PCnext), .b(32'h4), .out(PCnow));  // open: bin, bout
  Multiplexer #(.width(32), .enable("false")) multiplexer_4 (
    .in0(rs1data), .in1(PCnow), .out(multiplexer_4_out), .sel(Asel));
  Multiplexer #(.width(32), .enable("false")) multiplexer_5 (
    .in0(rs2data), .in1(imm), .out(multiplexer_5_out), .sel(Bsel));
  Comparator #(.width(32)) comparator_1 (
    .a(rs1data), .b(rs2data), .eq(comparator_1_eq), .lt(comparator_1_lt));  // open: gt
  Comparator #(.width(32), .mode("unsigned")) comparator_2 (
    .a(rs1data), .b(rs2data), .eq(comparator_2_eq), .lt(comparator_2_lt));  // open: gt
  Multiplexer #(.enable("false")) multiplexer_6 (.in0(comparator_1_lt), .in1(comparator_2_lt), .out(BrLT), .sel(BrUn));
  Multiplexer #(.enable("false")) multiplexer_7 (.in0(comparator_1_eq), .in1(comparator_2_eq), .out(BrEq), .sel(BrUn));
  alu Arithmetic_Logic_Unit (.A(multiplexer_4_out), .B(multiplexer_5_out), .ALUSel(ALUsel), .Result(ALUresult));
  regfile_main RegFile (
    .rs2(INSTRUCTION_t[24:20]), .rd(INSTRUCTION_t[11:7]), .Read_Data_1(rs1data), .Read_Data_2(rs2data),
    .ra(ra), .sp(sp), .t0(t0), .t1(t1), .t2(t2), .s0(s0), .s1(s1), .a0(a0), .rs1(INSTRUCTION_t[19:15]),
    .Write_Data(writeback), .RegWEn(RegWEn), .clk(CLOCK));

  // Other names for the same wires on the sheet: clk = CLOCK; fetch_addr[31:0] = FETCH_ADDRESS;
  //   INSTRUCTION_input[31:0] = INSTRUCTION; s2[31:0] = a0

  // Notes on the sheet:
  //   Output
  //   Inputs/Outputs from run.circ. DO NOT MOVE THESE.
  //   Inputs
  //   Inputs/Outputs from run.circ. DO NOT MOVE THESE.
endmodule

module control (
  input  [31:0] instr,
  input  BrLT,
  input  BrEq,
  output PCsel,
  output [2:0] Immsel,
  output RegWEn,
  output Asel,
  output Bsel,
  output [3:0] ALUsel,
  output MemRW,
  output [1:0] WBsel,
  output BrUn
);

  wire comparator_1_eq, comparator_2_eq, not_1_out, not_2_out, or_2_out;
  wire [0:0] control_word;
  wire [5:0] RV32_type;
  wire [11:0] multiplexer_1_out, multiplexer_2_out, multiplexer_3_out, multiplexer_4_out, multiplexer_5_out,
       multiplexer_6_out, multiplexer_7_out;

  Comparator #(.width(6)) comparator_1 (.a(6'b011100), .b(RV32_type), .eq(comparator_1_eq));  // open: gt, lt
  Comparator #(.width(6)) comparator_2 (.a(RV32_type), .b(6'b011110), .eq(comparator_2_eq));  // open: gt, lt
  Instr_type instr_type_1 (.instr(instr), .instr_type(RV32_type), .immediate(Immsel));
  or or_1 (BrUn, comparator_1_eq, comparator_2_eq);
  not not_1 (not_1_out, BrEq);
  or or_2 (or_2_out, BrEq, not_2_out);
  not not_2 (not_2_out, BrLT);
  Multiplexer #(.width(12), .enable("false")) multiplexer_1 (
    .in0(12'h404), .in1(12'hf32), .out(multiplexer_1_out), .sel(BrLT));
  Multiplexer #(.width(12), .enable("false")) multiplexer_2 (
    .in0(12'h405), .in1(12'hf33), .out(multiplexer_2_out), .sel(BrLT));
  Multiplexer #(.width(12), .enable("false")) multiplexer_3 (
    .in0(12'h404), .in1(12'hf32), .out(multiplexer_3_out), .sel(not_1_out));
  Multiplexer #(.width(12), .enable("false")) multiplexer_4 (
    .in0(12'h405), .in1(12'hf33), .out(multiplexer_4_out), .sel(or_2_out));
  Multiplexer #(.width(12), .enable("false")) multiplexer_5 (
    .in0(12'h404), .in1(12'hf32), .out(multiplexer_5_out), .sel(BrEq));
  Multiplexer #(.select(5), .width(12), .enable("false")) multiplexer_6 (
    .in0(12'h432), .in1(12'h452), .in2(12'h442), .in3(12'h4e2), .in4(12'h472), .in5(12'h462), .in6(12'h422),
    .in7(12'h492), .in8(12'h482), .in9(12'h4b2), .in10(12'h412), .in11(12'h4a2), .in12(12'h402),
    .in13(12'h530), .in14(12'h530), .in15(12'h530), .in16(12'h530), .in17(12'h530), .in18(12'h532),
    .in19(12'h5e2), .in20(12'h5d2), .in21(12'h522), .in22(12'h5b2), .in23(12'h512), .in24(12'h502),
    .in25(12'h138), .in26(multiplexer_5_out), .in27(multiplexer_1_out), .in28(multiplexer_2_out),
    .in29(multiplexer_3_out), .in30(multiplexer_4_out), .in31(12'h732), .out(multiplexer_6_out),
    .sel(RV32_type[4:0]));
  Multiplexer #(.select(2), .width(12), .enable("false")) multiplexer_7 (
    .in0(12'h7f2), .in1(12'hf34), .in2(12'hd32), .in3({12{1'b0}}), .out(multiplexer_7_out),
    .sel(RV32_type[1:0]));
  Multiplexer #(.width(12), .enable("false")) multiplexer_8 (
    .in0(multiplexer_6_out), .in1(multiplexer_7_out),
    .out({PCsel, RegWEn, Asel, Bsel, ALUsel, MemRW, WBsel, control_word[0]}), .sel(RV32_type[5]));

  // Other names for the same wires on the sheet: Br = BrUn;
  //   control_word[11:1] = {PCsel, RegWEn, Asel, Bsel, ALUsel, MemRW, WBsel}; Eq = BrEq; instruction[31:0] = instr;
  //   LT = BrLT
endmodule

module imm_gen (
  input  [31:0] Instr,
  input  [2:0] imm_sel,
  output [31:0] immediate
);

  wire [31:11] I_imm, S_imm;
  wire [31:12] B_imm;
  wire [31:20] J_imm;

  Multiplexer #(.width(21), .enable("false")) multiplexer_1 (
    .in0({21{1'b0}}), .in1({21{1'b1}}), .out(I_imm), .sel(Instr[31]));
  Multiplexer #(.width(21), .enable("false")) multiplexer_2 (
    .in0({21{1'b0}}), .in1({21{1'b1}}), .out(S_imm), .sel(Instr[31]));
  Multiplexer #(.width(20), .enable("false")) multiplexer_3 (
    .in0({20{1'b0}}), .in1({20{1'b1}}), .out(B_imm), .sel(Instr[31]));
  Multiplexer #(.width(12), .enable("false")) multiplexer_4 (
    .in0({12{1'b0}}), .in1({12{1'b1}}), .out(J_imm), .sel(Instr[31]));
  Multiplexer #(.select(3), .width(32), .enable("false")) multiplexer_5 (
    .in0({32{1'b0}}), .in1({I_imm, Instr[30:20]}), .in2({S_imm, Instr[30:25], Instr[11:7]}),
    .in3({B_imm, Instr[7], Instr[30:25], Instr[11:8], 1'b0}), .in4({Instr[31:12], {12{1'b0}}}),
    .in5({J_imm, Instr[19:12], Instr[20], Instr[30:21], 1'b0}), .in6({32{1'b0}}), .in7({32{1'b0}}),
    .out(immediate), .sel(imm_sel));

  // Other names for the same wires on the sheet: B_imm[11:1] = {Instr[7], Instr[30:25], Instr[11:8]};
  //   S_imm[10:0] = {Instr[30:25], Instr[11:7]}; Immsel[2:0] = imm_sel; I_imm[10:0] = Instr[30:20];
  //   J_imm[19:1] = {Instr[19:12], Instr[20], Instr[30:21]}; U_imm[31:12] = Instr[31:12]
endmodule

module Instr_type (
  input  [31:0] instr,
  output [5:0] instr_type,
  output [2:0] immediate
);

  wire add0, addi18, and12, andi24, auipc31, B, beq26, bgeu30, blt27, bltu28, bne29, div7, divu8, f3_0, f3_1,
       f3_2, f3_3, f3_4, f3_5, f3_6, f3_7, f7_0, f7_1, f7_2, I, I1, I2, I3, jal33, jalr34, lb13, lbu16, lh14,
       lhu17, lui32, lw15, mul1, mulh4, mulhu5, nor_1_out, nor_2_out, or10, or_3_out, or_4_out, ori23, R,
       remu11, S, sll3, slli19, slti20, srl9, srli22, sub2, sw25, U, U1, U2, UJ, xor6, xori21;

  Comparator #(.width(7)) comparator_1 (.a(instr[6:0]), .b(7'b0010111), .eq(U1));  // open: gt, lt
  Comparator #(.width(7)) comparator_2 (.a(instr[6:0]), .b(7'b0110111), .eq(U2));  // open: gt, lt
  Comparator #(.width(7)) comparator_3 (.a(instr[6:0]), .b(7'b1101111), .eq(UJ));  // open: gt, lt
  Comparator #(.width(7)) comparator_4 (.a(instr[6:0]), .b(7'b0110011), .eq(R));  // open: gt, lt
  Comparator #(.width(7)) comparator_5 (.a(instr[6:0]), .b(7'b0000011), .eq(I1));  // open: gt, lt
  Comparator #(.width(7)) comparator_6 (.a(instr[6:0]), .b(7'b0010011), .eq(I2));  // open: gt, lt
  Comparator #(.width(7)) comparator_7 (.a(instr[6:0]), .b(7'b1100111), .eq(I3));  // open: gt, lt
  Comparator #(.width(7)) comparator_8 (.a(instr[6:0]), .b(7'b0100011), .eq(S));  // open: gt, lt
  Comparator #(.width(7)) comparator_9 (.a(instr[6:0]), .b(7'b1100011), .eq(B));  // open: gt, lt
  assign immediate = R ? 3'b000 : 3'bz;  // Controlled_Buffer controlled_buffer_1
  assign immediate = I ? 3'b001 : 3'bz;  // Controlled_Buffer controlled_buffer_2
  assign immediate = S ? 3'b010 : 3'bz;  // Controlled_Buffer controlled_buffer_3
  assign immediate = B ? 3'b011 : 3'bz;  // Controlled_Buffer controlled_buffer_4
  assign immediate = U ? 3'b100 : 3'bz;  // Controlled_Buffer controlled_buffer_5
  assign immediate = UJ ? 3'b101 : 3'bz;  // Controlled_Buffer controlled_buffer_6
  nor nor_1 (nor_1_out, R, I, S, B, U, UJ);
  or or_1 (I, I1, I2, I3);
  assign immediate = nor_1_out ? 3'b110 : 3'bz;  // Controlled_Buffer controlled_buffer_7
  or or_2 (U, U1, U2);
  Comparator #(.width(3)) comparator_10 (.a(instr[14:12]), .b(3'b000), .eq(f3_0));  // open: gt, lt
  Comparator #(.width(3)) comparator_11 (.a(instr[14:12]), .b(3'b001), .eq(f3_1));  // open: gt, lt
  Comparator #(.width(3)) comparator_12 (.a(instr[14:12]), .b(3'b010), .eq(f3_2));  // open: gt, lt
  Comparator #(.width(3)) comparator_13 (.a(instr[14:12]), .b(3'b011), .eq(f3_3));  // open: gt, lt
  Comparator #(.width(3)) comparator_14 (.a(instr[14:12]), .b(3'b100), .eq(f3_4));  // open: gt, lt
  Comparator #(.width(3)) comparator_15 (.a(instr[14:12]), .b(3'b101), .eq(f3_5));  // open: gt, lt
  Comparator #(.width(3)) comparator_16 (.a(instr[14:12]), .b(3'b110), .eq(f3_6));  // open: gt, lt
  Comparator #(.width(3)) comparator_17 (.a(instr[14:12]), .b(3'b111), .eq(f3_7));  // open: gt, lt
  Comparator #(.width(7)) comparator_18 (.a(instr[31:25]), .b({7{1'b0}}), .eq(f7_0));  // open: gt, lt
  Comparator #(.width(7)) comparator_19 (.a(instr[31:25]), .b(7'b0000001), .eq(f7_1));  // open: gt, lt
  Comparator #(.width(7)) comparator_20 (.a(instr[31:25]), .b(7'b0100000), .eq(f7_2));  // open: gt, lt
  or or_3 (or_3_out, add0, mul1, sub2, sll3, mulh4, mulhu5, xor6, div7, divu8, srl9, or10, remu11, and12, lb13, lh14, lw15, lbu16, lhu17, addi18, slli19, slti20, xori21, srli22, ori23, andi24, sw25, beq26, blt27, bltu28, bne29, bgeu30, auipc31);
  or or_4 (or_4_out, lui32, jal33, jalr34);
  and and_1 (add0, R, f3_0, f7_0);
  and and_2 (mul1, R, f3_0, f7_1);
  and and_3 (sub2, R, f3_0, f7_2);
  and and_4 (sll3, R, f3_1, f7_0);
  and and_5 (mulh4, R, f3_1, f7_1);
  and and_6 (mulhu5, R, f3_3, f7_1);
  and and_7 (xor6, R, f3_4, f7_0);
  and and_8 (div7, R, f3_4, f7_1);
  and and_9 (divu8, R, f3_5, f7_1);
  nor nor_2 (nor_2_out, or_3_out, or_4_out);
  assign instr_type = nor_2_out ? 6'b100011 : 6'bz;  // Controlled_Buffer controlled_buffer_8
  and and_10 (srl9, R, f3_5, f7_0);
  and and_11 (or10, R, f3_6, f7_0);
  and and_12 (remu11, R, f3_7, f7_1);
  and and_13 (and12, R, f3_7, f7_0);
  and and_14 (lb13, I1, f3_0);
  and and_15 (lh14, I1, f3_1);
  and and_16 (lw15, I1, f3_2);
  and and_17 (lbu16, I1, f3_4);
  and and_18 (lhu17, I1, f3_5);
  and and_19 (addi18, I2, f3_0);
  and and_20 (slli19, I2, f3_1, f7_0);
  and and_21 (slti20, I2, f3_2);
  and and_22 (xori21, I2, f3_4);
  assign instr_type = add0 ? {6{1'b0}} : 6'bz;  // Controlled_Buffer controlled_buffer_9
  assign instr_type = mul1 ? 6'b000001 : 6'bz;  // Controlled_Buffer controlled_buffer_10
  assign instr_type = sub2 ? 6'b000010 : 6'bz;  // Controlled_Buffer controlled_buffer_11
  assign instr_type = sll3 ? 6'b000011 : 6'bz;  // Controlled_Buffer controlled_buffer_12
  assign instr_type = mulh4 ? 6'b000100 : 6'bz;  // Controlled_Buffer controlled_buffer_13
  assign instr_type = mulhu5 ? 6'b000101 : 6'bz;  // Controlled_Buffer controlled_buffer_14
  assign instr_type = xor6 ? 6'b000110 : 6'bz;  // Controlled_Buffer controlled_buffer_15
  and and_23 (srli22, I2, f3_5, f7_0);
  and and_24 (ori23, I2, f3_6);
  and and_25 (andi24, I2, f3_7);
  and and_26 (sw25, S, f3_2);
  assign instr_type = div7 ? 6'b000111 : 6'bz;  // Controlled_Buffer controlled_buffer_16
  assign instr_type = divu8 ? 6'b001000 : 6'bz;  // Controlled_Buffer controlled_buffer_17
  assign instr_type = srl9 ? 6'b001001 : 6'bz;  // Controlled_Buffer controlled_buffer_18
  assign instr_type = or10 ? 6'b001010 : 6'bz;  // Controlled_Buffer controlled_buffer_19
  assign instr_type = remu11 ? 6'b001011 : 6'bz;  // Controlled_Buffer controlled_buffer_20
  assign instr_type = and12 ? 6'b001100 : 6'bz;  // Controlled_Buffer controlled_buffer_21
  assign instr_type = lb13 ? 6'b001101 : 6'bz;  // Controlled_Buffer controlled_buffer_22
  and and_27 (beq26, B, f3_0);
  and and_28 (blt27, B, f3_4);
  and and_29 (bltu28, B, f3_6);
  and and_30 (bne29, B, f3_1);
  assign instr_type = lh14 ? 6'b001111 : 6'bz;  // Controlled_Buffer controlled_buffer_23
  assign instr_type = lw15 ? 6'b001111 : 6'bz;  // Controlled_Buffer controlled_buffer_24
  assign instr_type = lbu16 ? 6'b010000 : 6'bz;  // Controlled_Buffer controlled_buffer_25
  assign instr_type = lhu17 ? 6'b010001 : 6'bz;  // Controlled_Buffer controlled_buffer_26
  assign instr_type = addi18 ? 6'b010010 : 6'bz;  // Controlled_Buffer controlled_buffer_27
  assign instr_type = slli19 ? 6'b010011 : 6'bz;  // Controlled_Buffer controlled_buffer_28
  assign instr_type = slti20 ? 6'b010100 : 6'bz;  // Controlled_Buffer controlled_buffer_29
  and and_31 (bgeu30, B, f3_7);
  and and_32 (auipc31, U1, 1'b1);
  and and_33 (lui32, U2, 1'b1);
  and and_34 (jal33, UJ, 1'b1);
  assign instr_type = xori21 ? 6'b010101 : 6'bz;  // Controlled_Buffer controlled_buffer_30
  assign instr_type = srli22 ? 6'b010110 : 6'bz;  // Controlled_Buffer controlled_buffer_31
  assign instr_type = ori23 ? 6'b010111 : 6'bz;  // Controlled_Buffer controlled_buffer_32
  assign instr_type = andi24 ? 6'b011000 : 6'bz;  // Controlled_Buffer controlled_buffer_33
  assign instr_type = sw25 ? 6'b011001 : 6'bz;  // Controlled_Buffer controlled_buffer_34
  assign instr_type = beq26 ? 6'b011010 : 6'bz;  // Controlled_Buffer controlled_buffer_35
  assign instr_type = blt27 ? 6'b011011 : 6'bz;  // Controlled_Buffer controlled_buffer_36
  and and_35 (jalr34, I3, f3_0);
  assign instr_type = bltu28 ? 6'b011100 : 6'bz;  // Controlled_Buffer controlled_buffer_37
  assign instr_type = bne29 ? 6'b011101 : 6'bz;  // Controlled_Buffer controlled_buffer_38
  assign instr_type = bgeu30 ? 6'b011110 : 6'bz;  // Controlled_Buffer controlled_buffer_39
  assign instr_type = auipc31 ? 6'b011111 : 6'bz;  // Controlled_Buffer controlled_buffer_40
  assign instr_type = lui32 ? 6'b100000 : 6'bz;  // Controlled_Buffer controlled_buffer_41
  assign instr_type = jal33 ? 6'b100001 : 6'bz;  // Controlled_Buffer controlled_buffer_42
  assign instr_type = jalr34 ? 6'b100010 : 6'bz;  // Controlled_Buffer controlled_buffer_43

  // Other names for the same wires on the sheet: imm[2:0] = immediate; opcode[6:0] = instr[6:0];
  //   funct3[2:0] = instr[14:12]; funct7[6:0] = instr[31:25]; instr_sel[5:0] = instr_type
endmodule
